# Fritzing sketch Rosie (saved by Fritzing 0.9.3b)
circuit board: 9.52317cm x 9.931cm
breadboards: 1

parts:
  3v3 = female pin header, 15 pins [form="♀ (female)"]
  J2 = female pin header, 15 pins [form="♀ (female)"]
  SSR1 = IC, DIP package, 8 pins [chip_label=IC]
  5v+ = Screw terminal - 2 pins [package=THT]
  OP1 = IC, DIP package, 4 pins [chip_label=IC]
  OP2 = IC, DIP package, 4 pins [chip_label=IC]
  SSR2 = IC, DIP package, 8 pins [chip_label=IC]
  SSR3 = IC, DIP package, 8 pins [chip_label=IC]
  Feed_Sensor = screw terminal, 3 pins
  SSR4 = IC, DIP package, 8 pins [chip_label=IC]
  Seal_Heater = Screw terminal - 2 pins [package=THT]
  Cut_Heater = Screw terminal - 2 pins [package=THT]
  Feed_Motor = Screw terminal - 2 pins [package=THT]
  Cut_Motor = Screw terminal - 2 pins [package=THT]
  R1 = Resistor [tolerance=±5% resistance=220 package=THT]
  R2 = Resistor [tolerance=±5% resistance=220 package=THT]
  R3 = Resistor [tolerance=±5% resistance=220 package=THT]
  R4 = Resistor [tolerance=±5% resistance=220 package=THT]
  R5 = Resistor [tolerance=±5% resistance=220 package=THT]
  R6 = Resistor [tolerance=±5% resistance=220 package=THT]
  I/O = female pin header, 4 pins [form="♀ (female)"]
  R7 = Resistor [tolerance=±5% resistance=220 package=THT]
  LED1 = LED - 3mm [color="Red (633nm)" package="3 mm [THT]"]
  LED2 = LED - 3mm [color="Red (633nm)" package="3 mm [THT]"]
  LED3 = LED - 3mm [color="Red (633nm)" package="3 mm [THT]"]
  LED4 = LED - 3mm [color="Red (633nm)" package="3 mm [THT]"]
  D1 = Rectifier Diode [part_number=1N4001 package="300 mil [THT]"]
  R8 = Resistor [tolerance=±5% resistance=220 package=THT]
  R9 = Resistor [tolerance=±5% resistance=220 package=THT]
  R10 = Resistor [tolerance=±5% resistance=220 package=THT]
  R11 = Resistor [tolerance=±5% resistance=220 package=THT]
  Cut_Sensor = screw terminal, 3 pins

nets:
  N1: 3v3.pin4, Feed_Sensor.pin3
  N2: 3v3.pin6, OP1.pin4, R7.Pin_0
  N3: 3v3.pin7, OP2.pin2
  N4: 3v3.pin8, R1.Pin_1, R8.Pin_1
  N5: 3v3.pin10, Feed_Sensor.pin2, R6.Pin_0, R7.Pin_1, Cut_Sensor.pin2
  N6: 3v3.pin12, R2.Pin_1, R9.Pin_1
  N7: 3v3.pin13, R3.Pin_1, R10.Pin_1
  N8: 3v3.pin14, R4.Pin_1, R11.Pin_1
  N9: 3v3.pin15, Cut_Sensor.pin3
  N10: J2.pin1, 5v+.pin1
  N11: SSR1.pin2, R1.Pin_0
  N12: SSR1.pin5, Seal_Heater.pin2
  N13: SSR1.pin8, Seal_Heater.pin1
  N14: OP1.pin1, R5.Pin_0, D1.cathode
  N15: OP1.pin2, I/O.pin2, D1.anode
  N16: OP2.pin1, R6.Pin_1
  N17: OP2.pin3, I/O.pin3
  N18: OP2.pin4, I/O.pin4
  N19: SSR2.pin2, R2.Pin_0
  N20: SSR2.pin5, Cut_Heater.pin2
  N21: SSR2.pin8, Cut_Heater.pin1
  N22: SSR3.pin2, R3.Pin_0
  N23: SSR3.pin6, SSR3.pin7, Feed_Motor.pin2
  N24: SSR3.pin8, Feed_Motor.pin1
  N25: SSR4.pin2, R4.Pin_0
  N26: SSR4.pin5, SSR4.pin8, Cut_Motor.pin1
  N27: SSR4.pin6, SSR4.pin7, Cut_Motor.pin2
  N28: R5.Pin_1, I/O.pin1
  N29: LED1.anode, R8.Pin_0
  N30: LED2.anode, R9.Pin_0
  N31: LED3.anode, R10.Pin_0
  N32: LED4.anode, R11.Pin_0

notes:
  D0
  D2
  D4
  3v3
  Gnd
  D5
  D8
  Rx
  5v+
  NodeMCU
  r0sie
  S H G
  ⏦
  ⎓
  10A
  5A
  +
